// Logisim project part4.circ as structural Verilog: 1 circuit, main circuit main
module main (
  input  B0,
  input  B1,
  input  B2,
  input  B3,
  input  S0,
  input  S1,
  input  S2,
  input  S3,
  input  M,
  input  Cn,
  input  Clear
);

  wire n7404_1_p2, n7404_1_p4, n7404_1_p6, n7404_1_p10, n74174_1_p1, n74174_1_p2, n74174_1_p3, n74174_1_p9;

  // _7404 7404_1: pin names not known; wires that end beside it: B0, n7404_1_p2, B1, n7404_1_p4, B2, n7404_1_p6, 1'b0, 1'b1, B3, n7404_1_p10
  // DIP_74181 dip_74181_1: pin names not known; wires that end beside it: n7404_1_p2, S2, S2, S1, S0, Cn, M, n7404_1_p4, n7404_1_p6, n7404_1_p10
  // _74174 74174_1: pin names not known; wires that end beside it: n74174_1_p1, n74174_1_p2, n74174_1_p3, Clear, n74174_1_p1, n74174_1_p2, n74174_1_p3, 1'b0, n74174_1_p9, 1'b1, n74174_1_p9
endmodule
